# Fritzing sketch connection (saved by Fritzing 0.9.0b)

parts:
  Raspberry_Pi_B_rev1 = Raspberry Pi B rev2
  U1 = XBEE-1 [package=xbee-1]

nets:
  3V3: Raspberry_Pi_B_rev1.3V3, Raspberry_Pi_B_rev1.GPIO_3, U1.VDD
  N1: Raspberry_Pi_B_rev1.GPIO_14, U1.DIN
  N2: Raspberry_Pi_B_rev1.GPIO_15, U1.DOUT
  GND: Raspberry_Pi_B_rev1.GND, U1.GND
